// Logisim project cpu.circ as structural Verilog: 1 circuit, main circuit cpu
module cpu (
  input  clk,
  input  [31:0] INSTRUCTION,
  input  [31:0] READ_DATA,
  input  [3:0] in_4,
  input  [1:0] in_5,
  output [31:0] WRITE_ADDRESS,
  output [31:0] PROGRAM_COUNTER,
  output [31:0] ra,
  output [31:0] sp,
  output [31:0] t0,
  output [31:0] t1,
  output [31:0] t2,
  output [31:0] s0,
  output [31:0] s1,
  output [31:0] a0,
  output [31:0] tohost,
  output [3:0] WRITE_ENABLE,
  output [31:0] WRITE_DATA
);

  wire [2:0] funct3;
  wire [11:0] imm12;
  wire [19:0] INSTRUCTION_IN;
  wire [31:0] alu_1_result, imm, PC4, rs1_data, Write_Data_t;

  Adder #(.width(32)) adder_1 (.a(PROGRAM_COUNTER), .b(32'h4), .out(PC4));  // open: cin, cout
  Register #(.width(32)) PC (.D(PC4), .clk(clk), .Q(PROGRAM_COUNTER));  // open: en, clr
  Register #(.width(32)) register_1 (
    .D(INSTRUCTION), .clk(clk), .Q({imm12, INSTRUCTION_IN[19:15], funct3, INSTRUCTION_IN[11:0]}));  // open: en, clr
  // control_logic control_logic_1: pin names not known
  imm_gen imm_gen_1 (.inst({imm12, INSTRUCTION_IN[19:15], funct3, INSTRUCTION_IN[11:0]}), .ImmSel(funct3), .imm(imm));
  regfile regfile_1 (
    .rs1(INSTRUCTION_IN[19:15]), .rd(INSTRUCTION_IN[11:7]), .Write_Data(Write_Data_t), .RegWEn(1'b1),
    .clk(clk), .ra(ra), .sp(sp), .t0(t0), .t1(t1), .t2(t2), .s0(s0), .s1(s1), .a0(a0), .Read_Data_1(rs1_data));  // open: rs2, Read_Data_2
  // branch_comp branch_comp_1: pin names not known
  alu alu_1 (.Result(alu_1_result), .A(rs1_data), .B(imm), .ALUSel(in_4));
  csr csr_1 (.tohost(tohost));  // open: CSR_address, CSR_din, CSR_WE, clk
  Multiplexer #(.enable("false"), .select(2), .width(32)) multiplexer_1 (
    .in0(alu_1_result), .in1(READ_DATA), .in2(PC4), .out(Write_Data_t), .sel(in_5));  // open: in3

  // Other names for the same wires on the sheet: opcode[6:0] = INSTRUCTION_IN[6:0]; rd[4:0] = INSTRUCTION_IN[11:7];
  //   INSTRUCTION_IN (some bits) = {imm12, funct3}; rs1[4:0] = INSTRUCTION_IN[19:15]; WBSEL[1:0] = in_5

  // Notes on the sheet:
  //   Output to IMEM
  //   IMEM (do **NOT** move this)
  //   Inputs from IMEM
  //   It is OK to move the PC, RegFile, ALU, MEM, Branch Comp, Imm Gen, and Control Logic to wherever is most convenient for you when constructing your CPU, and to delete this text
  //   Inputs/Outputs for testing. Do **NOT** move these.
  //   Outputs To DMEM
  //   DMEM (do **NOT** move this)
  //   Inputs From DMEM
endmodule
